# Fritzing sketch draft (saved by Fritzing 0.8.7b)

parts:
  Componente1 = Arduino Uno (Rev3)  # not connected
  Componente2 = Arduino Prototyping Shield
  RF_Receiver1 = RF_Receiver
  RF_Sender_433_Mhz1 = RF Sender
  LED1 = LED - 5mm [color="Red (633nm)" package="5 mm [THT]"]
  LED3 = LED - 5mm [color="Yellow (595nm)" package="5 mm [THT]"]
  LED4 = LED - 5mm [color="Infrared (940nm)" package="5 mm [THT]"]
  LED5 = LED - 5mm [color="Infrared (940nm)" package="5 mm [THT]"]
  LED2 = LED - 5mm [color="Green (555nm)" package="5 mm [THT]"]
  R1 = Resistor [tolerance=±5% resistance=82 package=THT]
  NPN_Transistor1 = NPN-Transistor [package="TO92 [THT]"]
  IR1 = TSOP312.., 314.. [package=THT]
  R3 = Resistor [tolerance=±5% resistance=82 package=THT]
  R4 = Resistor [tolerance=±5% resistance=33k package=THT]
  R5 = Resistor [tolerance=±5% resistance=82 package=THT]
  R6 = Resistor [tolerance=±5% resistance=270 package=THT]

nets:
  GND: Componente2.GND, Componente2.N$235, Componente2.N$324, Componente2.N$325, Componente2.N$362, Componente2.N$367, Componente2.N$377, Componente2.N$378, RF_Receiver1.GND, RF_Sender_433_Mhz1.GND, LED1.cathode, LED3.cathode, LED2.cathode, NPN_Transistor1.E, IR1.GND
  N1: Componente2.D8, Componente2.N$411, R4.Pin_1
  N2: Componente2.D0(RX), IR1.Data
  N3: Componente2.D2, RF_Receiver1.DIN
  N4: Componente2.D3, Componente2.N$395, R3.Pin_1
  N5: Componente2.D5, Componente2.N$16, RF_Sender_433_Mhz1.DIN
  N6: Componente2.D6, Componente2.N$420, R1.Pin_1
  N7: Componente2.D7, Componente2.N$413, R5.Pin_1
  VIN: Componente2.+5V, Componente2.N$105, Componente2.N$281, Componente2.N$314, Componente2.N$321, RF_Receiver1.VIN, RF_Sender_433_Mhz1.VIN, IR1.Vs
  N8: Componente2.+9V, Componente2.N$356, R6.Pin_1
  N9: Componente2.N$81, LED4.cathode, LED5.cathode, NPN_Transistor1.C
  N10: Componente2.N$320, Componente2.N$379, NPN_Transistor1.B, R3.Pin_0
  N11: Componente2.N$402, LED2.anode, R4.Pin_0
  N12: Componente2.N$406, LED1.anode, R5.Pin_0
  N13: Componente2.N$424, LED3.anode, R1.Pin_0
  N14: LED4.anode, LED5.anode, R6.Pin_0

custom parts:
  TSOP312.., 314..: The TSOP312.., TSOP314.. series are miniaturized receivers for infrared remote control systems. A PIN diode and a preamplifier are assembled on a lead frame, the epoxy package acts as an IR filter. The demodulated output signal can be directly decoded by a microprocessor. The TSOP312.. is compatible with all common IR remote control data formats. The TSOP314.. is optimized to suppress almost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
